# Fritzing sketch pianoDiagram (saved by Fritzing 0.8.7b)
breadboards: 1

parts:
  Part1 = Arduino MP3 Player Shield
  Intel(R)_Galileo_1 = Intel(R) Galileo  # not connected
  MCP23S1 = MCP23S17 [package="28-pin PDIP"]

nets:
  N1: Part1.3.3, MCP23S1.V_dd, MCP23S1.RESET
  N2: Part1.D10, MCP23S1.CS
  N3: Part1.5V-MOSI, MCP23S1.SI
  N4: Part1.5V-SCK, MCP23S1.SCK
  N5: Part1.GND, MCP23S1.V_ss, MCP23S1.A0, MCP23S1.A1, MCP23S1.A2

custom parts:
  Intel(R) Galileo: Galileo is a microcontroller board based on the Intel® Quark SoC X1000 Application Processor, a 32-bit Intel Pentium-class system on a chip (datasheet). It’s the first board based on Intel® architecture designed to be hardware and software pin-compatible with Arduino shields designed for the Uno R3. Digital pins 0 to 13 (and the adjacent AREF and GND pins), Analog inputs 0 to 5, the power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
  MCP23S17: 16-bit input/output port expander with interrupt output Cascadable for up to 8 devices on one bus 25mA sink/source capability per I/O Supports up to 10MHz SPI™ clock speeds
